# Fritzing sketch Untitled Sketch (saved by Fritzing 1.0.1rc)

parts:
  A1 = Esp32-c3 super mini
  Q1 = Basic FET N-Channel [package="TO220 [THT]"]
  L1 = Solenoid
  R1 = Resistor [tolerance=±5% resistance=220 package="2512 [SMD]"]
  J1 = USB type C-05-power-only

nets:
  N1: A1.Pin_11, R1.Pin_0
  N2: A1.Pin_15, Q1.source, J1.Pin_3
  N3: A1.Pin_16, L1.pin2, J1.Pin_2
  N4: Q1.gate, R1.Pin_1
  N5: Q1.drain, L1.pin1

custom parts:
  Esp32-c3 super mini: ESP32-C3 Development Board ESP32 SuperMini Development Board ESP32 Development Board WiFi Bluetooth.
